# Fritzing sketch Board_Layout (saved by Fritzing 0.9.3b)
circuit board: 8.46667cm x 5.64444cm
breadboards: 3

parts:
  U1 = ESP32-38PinWide [part_number=ESP32-38PinWide]
  Part1 = Logic Level Converter
  J1 = Power Jack [package=power_jack_combo]

nets:
  N1: U1.3.3, Part1.LV
  N2: U1.GPIO26, Part1.TX_LV
  GND: U1.GND, Part1.GND, J1.GND
  N3: U1.VIN, Part1.HV

custom parts:
  ESP32-38PinWide: Generic 38-Pin ESP32 with wide format (only access to one side of pins on a breadboard) based on Stephen Lilley's HiLetgo ESP-WROOM-32 ESP32 ESP-32S Development Board.
